# Fritzing sketch fight-vest-scatch (saved by Fritzing 0.9.3b)
breadboards: 1

parts:
  Part1 = Arduino Uno (Rev3)
  Part2 = Bluetooth HC-05 Macho
  VCC1 = Battery block 9V

nets:
  N1: Part1.D0/RX, Part2.TXD
  N2: Part1.D1/TX, Part2.RXD
  5V: Part1.5V, Part2.VCC
  GND: Part1.GND, Part2.GND, VCC1.-
  N3: Part1.VIN, VCC1.+
